// Logisim project Cache.circ as structural Verilog: 8 circuits, main circuit implementation
module implementation (
  input  [9:0] CpuAddressIn,
  input  CpuReadIn,
  input  CpuWriteIn,
  input  [7:0] CpuWriteValueIn,
  input  [31:0] LineFromMemIn,
  input  ClkIn,
  output ReadyOut,
  output DidContainOut,
  output [7:0] ByteReadOut,
  output [7:0] MemAddressOut,
  output MemReadOut,
  output MemWriteOut,
  output [31:0] Line2MemOut
);

  wire and_1_out, and_2_out, and_3_out, and_4_out, Contain0, Contain1, DidContain, Dirty, Dirty0, Dirty1,
       EnableValue, fsmRead0, fsmRead1, fsmWrite0, fsmWrite1, IsInit, multiplexer_1_out, multiplexer_2_out,
       or_1_out, or_2_out, or_3_out, or_4_out, SaveCpuWrite, SavedCpuRead, UpdateAge, updateAge0, updateAge1;
  wire [1:0] Offset;
  wire [6:0] CPUTag, WriteToTag, WriteToTag0, WriteToTag1;
  wire [7:0] ByteRead0, ByteRead1, SavedWriteValue, SelectedSetByteRead;
  wire [31:0] Line2Mem0, Line2Mem1;

  or or_1 (or_1_out, CpuWriteIn, CpuReadIn);
  or or_2 (or_2_out, CpuWriteIn, CpuReadIn);
  or or_3 (or_3_out, CpuWriteIn, CpuReadIn);
  or or_4 (or_4_out, CpuWriteIn, CpuReadIn);
  and and_1 (and_1_out, ReadyOut, or_1_out);
  and and_2 (and_2_out, ReadyOut, or_2_out);
  and and_3 (and_3_out, ReadyOut, or_3_out);
  and and_4 (and_4_out, ReadyOut, or_4_out);
  Register #(.width(1)) register_1 (.D(CpuReadIn), .en(and_1_out), .clk(ClkIn), .Q(SavedCpuRead));  // open: clr
  Register #(.width(1)) register_2 (.D(CpuWriteIn), .en(and_2_out), .clk(ClkIn), .Q(SaveCpuWrite));  // open: clr
  Register register_3 (.D(CpuWriteValueIn), .en(and_3_out), .clk(ClkIn), .Q(SavedWriteValue));  // open: clr
  Demultiplexer #(.enable("false")) demultiplexer_1 (
    .out0(fsmRead0), .out1(fsmRead1), .in(MemReadOut), .sel(MemAddressOut[0]));
  Demultiplexer #(.enable("false")) demultiplexer_2 (
    .out0(fsmWrite0), .out1(fsmWrite1), .in(MemWriteOut), .sel(MemAddressOut[0]));
  Demultiplexer #(.enable("false")) demultiplexer_3 (
    .out0(updateAge0), .out1(updateAge1), .in(UpdateAge), .sel(MemAddressOut[0]));
  Register #(.width(10)) register_4 (
    .D(CpuAddressIn), .en(and_4_out), .clk(ClkIn), .Q({CPUTag, MemAddressOut[0], Offset}));  // open: clr
  Multiplexer #(.enable("false")) multiplexer_1 (
    .in0(SavedCpuRead), .in1(CpuReadIn), .out(multiplexer_1_out), .sel(ReadyOut));
  Multiplexer #(.enable("false")) multiplexer_2 (
    .in0(SaveCpuWrite), .in1(CpuReadIn), .out(multiplexer_2_out), .sel(ReadyOut));
  fsm fsm_1 (
    .DirtyIn(Dirty), .ContainIn(DidContain), .CpuReadIn(multiplexer_1_out), .CpuWriteIn(multiplexer_2_out),
    .ClkIn(ClkIn), .ReadyOut(ReadyOut), .MemReadOut(MemReadOut), .MemWriteOut(MemWriteOut),
    .UpdateAgeOut(UpdateAge), .IsInitOut(IsInit), .EnableValueOut(EnableValue));
  Set Set0 (
    .LineFromMemIn(LineFromMemIn), .CpuWriteValueIn(CpuWriteValueIn), .ValueEnable(EnableValue),
    .CpuTagIn(CPUTag), .OffsetIn(Offset), .fsmReadIn(fsmRead0), .fsmWriteIn(fsmWrite0),
    .UpdateAgeIn(updateAge0), .isInitIn(IsInit), .ClkIn(ClkIn), .ContainsOut(Contain0),
    .ByteReadOut(ByteRead0), .Line2MemOut(Line2Mem0), .DirtyOut(Dirty0), .CpuTagWriteOut(WriteToTag0));
  Set Set1 (
    .LineFromMemIn(LineFromMemIn), .CpuWriteValueIn(CpuWriteValueIn), .ValueEnable(EnableValue),
    .CpuTagIn(CPUTag), .OffsetIn(Offset), .fsmReadIn(fsmRead1), .fsmWriteIn(fsmWrite1),
    .UpdateAgeIn(updateAge1), .isInitIn(IsInit), .ClkIn(ClkIn), .ContainsOut(Contain1),
    .ByteReadOut(ByteRead1), .Line2MemOut(Line2Mem1), .DirtyOut(Dirty1), .CpuTagWriteOut(WriteToTag1));
  Multiplexer #(.enable("false")) multiplexer_3 (
    .in0(Contain0), .in1(Contain1), .out(DidContain), .sel(MemAddressOut[0]));
  Multiplexer #(.enable("false"), .width(8)) multiplexer_4 (
    .in0(ByteRead0), .in1(ByteRead1), .out(SelectedSetByteRead), .sel(MemAddressOut[0]));
  Multiplexer #(.enable("false"), .width(32)) multiplexer_5 (
    .in0(Line2Mem0), .in1(Line2Mem1), .out(Line2MemOut), .sel(MemAddressOut[0]));
  Multiplexer #(.enable("false")) multiplexer_6 (.in0(Dirty0), .in1(Dirty1), .out(Dirty), .sel(MemAddressOut[0]));
  Multiplexer #(.enable("false"), .width(7)) multiplexer_7 (
    .in0(WriteToTag0), .in1(WriteToTag1), .out(WriteToTag), .sel(MemAddressOut[0]));
  Register #(.width(1)) register_5 (.D(DidContain), .en(ReadyOut), .clk(ClkIn), .Q(DidContainOut));  // open: clr
  Multiplexer #(.enable("false"), .width(7)) multiplexer_8 (
    .in0(CPUTag), .in1(WriteToTag), .out(MemAddressOut[7:1]), .sel(MemWriteOut));
  Register register_6 (.D(SelectedSetByteRead), .en(ReadyOut), .clk(ClkIn), .Q(ByteReadOut));  // open: clr

  // Other names for the same wires on the sheet: ByteRead[7:0] = ByteReadOut; clk = ClkIn;
  //   CpuAddress[9:0] = CpuAddressIn; CpuRead = CpuReadIn; CpuWrite = CpuWriteIn;
  //   CpuWriteValue[7:0] = CpuWriteValueIn; fsmRead = MemReadOut; MemRead = MemReadOut; fsmWrite = MemWriteOut;
  //   MemWrite = MemWriteOut; LineFromMem[31:0] = LineFromMemIn; MemAddress[7:0] = MemAddressOut;
  //   SavedCpuAddress[9:0] = {CPUTag, MemAddressOut[0], Offset}; Setbit = MemAddressOut[0]; Ready = ReadyOut;
  //   ReportingContains = DidContainOut; Line2Mem[31:0] = Line2MemOut; SelectedSetLine2Mem[31:0] = Line2MemOut

  // Notes on the sheet:
  //   Enable bit should be: SaveContains
endmodule

module Set (
  input  [31:0] LineFromMemIn,
  input  [7:0] CpuWriteValueIn,
  input  ValueEnable,
  input  [6:0] CpuTagIn,
  input  [1:0] OffsetIn,
  input  fsmReadIn,
  input  fsmWriteIn,
  input  UpdateAgeIn,
  input  isInitIn,
  input  ClkIn,
  output ContainsOut,
  output [7:0] ByteReadOut,
  output [31:0] Line2MemOut,
  output DirtyOut,
  output [6:0] CpuTagWriteOut
);

  wire Dirty0, Dirty1, Dirty2, fsmRead0, fsmRead1, fsmRead2, fsmWrite0, fsmWrite1, fsmWrite2, isContainWay0,
       isContainWay1, isContainWay2, isOldest0, isOldest1, isOldest2, UpdateAge0, UpdateAge1, UpdateAge2,
       ValidEnable0, ValidEnable1, ValidEnable2;
  wire [1:0] AgeAccessed, AgeAccessed0, AgeAccessed1, AgeAccessed2, AgeIn0, AgeIn1, AgeIn2, ContainIndex,
       multiplexer_1_out, OldestIndex;
  wire [6:0] Tag0, Tag1, Tag2;
  wire [7:0] ByteRead0, ByteRead1, ByteRead2;
  wire [31:0] Line2Mem0, Line2Mem1, Line2Mem2;

  Demultiplexer #(.enable("false"), .select(2)) demultiplexer_1 (
    .out0(fsmRead0), .out1(fsmRead1), .out2(fsmRead2), .in(fsmReadIn), .sel(OldestIndex));  // open: out3
  Demultiplexer #(.enable("false"), .select(2)) demultiplexer_2 (
    .out0(fsmWrite0), .out1(fsmWrite1), .out2(fsmWrite2), .in(fsmWriteIn), .sel(ContainIndex));  // open: out3
  Demultiplexer #(.enable("false"), .select(2)) demultiplexer_3 (
    .out0(ValidEnable0), .out1(ValidEnable1), .out2(ValidEnable2), .in(ValueEnable), .sel(ContainIndex));  // open: out3
  Demultiplexer #(.enable("false"), .select(2)) demultiplexer_4 (
    .out0(UpdateAge0), .out1(UpdateAge1), .out2(UpdateAge2), .in(UpdateAgeIn), .sel(ContainIndex));  // open: out3
  Multiplexer #(.enable("false"), .select(2), .width(2)) multiplexer_1 (
    .in0(AgeAccessed0), .in1(AgeAccessed1), .in2(AgeAccessed2), .out(multiplexer_1_out), .sel(ContainIndex));  // open: in3
  Multiplexer #(.enable("false"), .width(2)) multiplexer_2 (
    .in0(AgeAccessed0), .in1(2'b00), .out(AgeIn0), .sel(isInitIn));
  Multiplexer #(.enable("false"), .width(2)) multiplexer_3 (
    .in0(AgeAccessed1), .in1(2'b01), .out(AgeIn1), .sel(isInitIn));
  Multiplexer #(.enable("false"), .width(2)) multiplexer_4 (
    .in0(AgeAccessed2), .in1(2'b10), .out(AgeIn2), .sel(isInitIn));
  Multiplexer #(.enable("false"), .width(2)) multiplexer_5 (
    .in0(2'b10), .in1(multiplexer_1_out), .out(AgeAccessed), .sel(ContainsOut));
  Way Way0 (
    .LineFromMemIn(LineFromMemIn), .AgeIn(AgeIn0), .CpuTagIn(CpuTagIn), .OffsetIn(OffsetIn),
    .fsmReadIn(fsmRead0), .fsmWriteIn(fsmWrite0), .ValueEnable(ValidEnable0), .UpdateAgeIn(UpdateAge0),
    .ClkIn(ClkIn), .CpuWriteValueIn(CpuWriteValueIn), .ContainsOut(isContainWay0), .ByteReadOut(ByteRead0),
    .isOldestOut(isOldest0), .AgeAccessed(AgeAccessed0), .Line2MemOut(Line2Mem0), .DirtyOut(Dirty0),
    .TagOut(Tag0));
  Way way_1 (
    .LineFromMemIn(LineFromMemIn), .AgeIn(AgeIn0), .CpuTagIn(CpuTagIn), .OffsetIn(OffsetIn),
    .fsmReadIn(fsmRead1), .fsmWriteIn(fsmWrite1), .ValueEnable(ValidEnable1), .UpdateAgeIn(UpdateAge1),
    .ClkIn(ClkIn), .CpuWriteValueIn(CpuWriteValueIn), .ContainsOut(isContainWay1), .ByteReadOut(ByteRead1),
    .isOldestOut(isOldest1), .AgeAccessed(AgeAccessed1), .Line2MemOut(Line2Mem1), .DirtyOut(Dirty1),
    .TagOut(Tag1));
  Way way_2 (
    .LineFromMemIn(LineFromMemIn), .AgeIn(AgeIn0), .CpuTagIn(CpuTagIn), .OffsetIn(OffsetIn),
    .fsmReadIn(fsmRead2), .fsmWriteIn(fsmWrite2), .ValueEnable(ValidEnable2), .UpdateAgeIn(UpdateAge2),
    .ClkIn(ClkIn), .CpuWriteValueIn(CpuWriteValueIn), .ContainsOut(isContainWay2), .ByteReadOut(ByteRead2),
    .isOldestOut(isOldest2), .AgeAccessed(AgeAccessed2), .Line2MemOut(Line2Mem2), .DirtyOut(Dirty2),
    .TagOut(Tag2));
  // Probe on ContainIndex
  BitFinder #(.width(3)) bitfinder_1 (
    .in({isContainWay2, isContainWay1, isContainWay0}), .index(ContainIndex), .found(ContainsOut));
  // Probe on ContainsOut
  // Probe on OldestIndex
  BitFinder #(.width(3)) bitfinder_2 (.in({isOldest2, isOldest1, isOldest0}), .index(OldestIndex));  // open: found
  Multiplexer #(.enable("false"), .select(2), .width(8)) multiplexer_6 (
    .in0(ByteRead0), .in1(ByteRead1), .in2(ByteRead2), .out(ByteReadOut), .sel(ContainIndex));  // open: in3
  Multiplexer #(.enable("false"), .select(2)) multiplexer_7 (
    .in0(Dirty0), .in1(Dirty1), .in2(Dirty2), .out(DirtyOut), .sel(OldestIndex));  // open: in3
  Multiplexer #(.enable("false"), .select(2), .width(7)) multiplexer_8 (
    .in0(Tag0), .in1(Tag1), .in2(Tag2), .out(CpuTagWriteOut), .sel(ContainIndex));  // open: in3
  Multiplexer #(.enable("false"), .select(2), .width(32)) multiplexer_9 (
    .in0(Line2Mem0), .in1(Line2Mem1), .in2(Line2Mem2), .out(Line2MemOut), .sel(ContainIndex));  // open: in3

  // Other names for the same wires on the sheet: ByteRead[7:0] = ByteReadOut; clk = ClkIn; CpuTag[6:0] = CpuTagIn;
  //   CpuWriteValue[7:0] = CpuWriteValueIn; Dirty = DirtyOut; fsmRead = fsmReadIn; fsmWrite = fsmWriteIn;
  //   isContain = ContainsOut; isInit = isInitIn; Line2Mem[31:0] = Line2MemOut; LineFromMem[31:0] = LineFromMemIn;
  //   Offset[1:0] = OffsetIn; TagOutToWrite[6:0] = CpuTagWriteOut; UpdateAge = UpdateAgeIn; ValidEnable = ValueEnable
endmodule

module Way (
  input  [31:0] LineFromMemIn,
  input  [1:0] AgeIn,
  input  [6:0] CpuTagIn,
  input  [1:0] OffsetIn,
  input  fsmReadIn,
  input  fsmWriteIn,
  input  ValueEnable,
  input  UpdateAgeIn,
  input  ClkIn,
  input  [7:0] CpuWriteValueIn,
  output ContainsOut,
  output [7:0] ByteReadOut,
  output isOldestOut,
  output [1:0] AgeAccessed,
  output [31:0] Line2MemOut,
  output DirtyOut,
  output [6:0] TagOut
);

  wire comparator_1_eq, DirtyEnable, multiplexer_1_out, multiplexer_3_out, ValidBit;
  wire [1:0] multiplexer_2_out, NewAge;

  Multiplexer #(.enable("false")) multiplexer_1 (.in1(1'b0), .out(multiplexer_1_out), .sel(fsmReadIn));  // open: in0
  Register #(.width(7)) register_1 (.D(CpuTagIn), .en(fsmReadIn), .clk(ClkIn), .Q(TagOut));  // open: clr
  Register #(.width(1)) Valid (.D(fsmReadIn), .en(fsmReadIn), .clk(ClkIn), .Q(ValidBit));  // open: clr
  Multiplexer #(.enable("false"), .width(2)) multiplexer_2 (
    .in0(AgeIn), .in1(NewAge), .out(multiplexer_2_out), .sel(UpdateAgeIn));
  Multiplexer #(.enable("false")) multiplexer_3 (
    .in0(multiplexer_1_out), .in1(1'b1), .out(multiplexer_3_out), .sel(fsmWriteIn));
  Register #(.width(2)) Age (.D(multiplexer_2_out), .en(UpdateAgeIn), .clk(ClkIn), .Q(AgeAccessed));  // open: clr
  Register #(.width(1)) Dirty (.D(multiplexer_3_out), .en(DirtyEnable), .clk(ClkIn), .Q(DirtyOut));  // open: clr
  Comparator #(.mode("unsigned"), .width(7)) comparator_1 (
    .a(CpuTagIn), .b(TagOut), .eq(comparator_1_eq));  // open: gt, lt
  UpdateAges updateages_1 (.AgeOfThisWayIn(AgeAccessed), .AgeOfWayAccessedIn(AgeIn), .NewAgeOut(NewAge));
  BlockCirc blockcirc_1 (
    .LineFromMemIn(LineFromMemIn), .CpuWriteValueIn(CpuWriteValueIn), .enableValueIn(ValueEnable),
    .fsmReadIn(fsmReadIn), .OffsetIn(OffsetIn), .DirtyIn(DirtyOut), .ClkIn(ClkIn), .ByteReadOut(ByteReadOut),
    .Line2MemOut(Line2MemOut));
  and and_1 (ContainsOut, comparator_1_eq, ValidBit);
  Comparator #(.mode("unsigned"), .width(2)) comparator_2 (
    .a(2'b10), .b(AgeAccessed), .eq(isOldestOut));  // open: gt, lt

  // Other names for the same wires on the sheet: AgeOut[1:0] = AgeAccessed; AgeWayAccessed[1:0] = AgeIn;
  //   ByteRead[7:0] = ByteReadOut; clk = ClkIn; Contains = ContainsOut; CpuTag[6:0] = CpuTagIn;
  //   CpuWriteValue[7:0] = CpuWriteValueIn; DirtyBit = DirtyOut; fsmRead = fsmReadIn; fsmWrite = fsmWriteIn;
  //   isOldest = isOldestOut; Line2Mem[31:0] = Line2MemOut; LineFromMem[31:0] = LineFromMemIn; Offset[1:0] = OffsetIn;
  //   Tag[6:0] = TagOut; UpdateAge = UpdateAgeIn
endmodule

module BlockCirc (
  input  [31:0] LineFromMemIn,
  input  [7:0] CpuWriteValueIn,
  input  enableValueIn,
  input  fsmReadIn,
  input  [1:0] OffsetIn,
  input  DirtyIn,
  input  ClkIn,
  output [7:0] ByteReadOut,
  output [31:0] Line2MemOut
);

  wire Reg_Write0, Reg_Write1, Reg_Write2, Reg_Write3;
  wire [7:0] multiplexer_1_out, multiplexer_2_out, multiplexer_3_out, multiplexer_4_out, multiplexer_5_out,
       multiplexer_6_out, multiplexer_7_out, multiplexer_8_out;

  Demultiplexer #(.enable("false"), .select(2)) demultiplexer_1 (
    .out0(Reg_Write0), .out1(Reg_Write1), .out2(Reg_Write2), .out3(Reg_Write3), .in(DirtyIn), .sel(OffsetIn));
  Multiplexer #(.enable("false"), .width(8)) multiplexer_1 (
    .in0(LineFromMemIn[7:0]), .in1(CpuWriteValueIn), .out(multiplexer_1_out), .sel(Reg_Write0));
  Multiplexer #(.enable("false"), .width(8)) multiplexer_2 (
    .in0(LineFromMemIn[15:8]), .in1(CpuWriteValueIn), .out(multiplexer_2_out), .sel(Reg_Write1));
  Multiplexer #(.enable("false"), .width(8)) multiplexer_3 (
    .in0(LineFromMemIn[23:16]), .in1(CpuWriteValueIn), .out(multiplexer_3_out), .sel(Reg_Write2));
  Multiplexer #(.enable("false"), .width(8)) multiplexer_4 (
    .in0(LineFromMemIn[31:24]), .in1(CpuWriteValueIn), .out(multiplexer_4_out), .sel(Reg_Write3));
  Multiplexer #(.enable("false"), .width(8)) multiplexer_5 (
    .in0(multiplexer_3_out), .in1(LineFromMemIn[23:16]), .out(multiplexer_5_out), .sel(fsmReadIn));
  Multiplexer #(.enable("false"), .width(8)) multiplexer_6 (
    .in0(multiplexer_4_out), .in1(LineFromMemIn[31:24]), .out(multiplexer_6_out), .sel(fsmReadIn));
  Multiplexer #(.enable("false"), .width(8)) multiplexer_7 (
    .in0(multiplexer_1_out), .in1(LineFromMemIn[7:0]), .out(multiplexer_7_out), .sel(fsmReadIn));
  Multiplexer #(.enable("false"), .width(8)) multiplexer_8 (
    .in0(multiplexer_2_out), .in1(LineFromMemIn[15:8]), .out(multiplexer_8_out), .sel(fsmReadIn));
  Register register_1 (.D(multiplexer_7_out), .en(enableValueIn), .clk(ClkIn), .Q(Line2MemOut[7:0]));  // open: clr
  Register register_2 (.D(multiplexer_8_out), .en(enableValueIn), .clk(ClkIn), .Q(Line2MemOut[15:8]));  // open: clr
  Register register_3 (.D(multiplexer_5_out), .en(enableValueIn), .clk(ClkIn), .Q(Line2MemOut[23:16]));  // open: clr
  Register register_4 (.D(multiplexer_6_out), .en(enableValueIn), .clk(ClkIn), .Q(Line2MemOut[31:24]));  // open: clr
  Multiplexer #(.enable("false"), .select(2), .width(8)) multiplexer_9 (
    .in0(Line2MemOut[7:0]), .in1(Line2MemOut[15:8]), .in2(Line2MemOut[23:16]), .in3(Line2MemOut[31:24]),
    .out(ByteReadOut), .sel(OffsetIn));
  // Probe on Line2MemOut

  // Other names for the same wires on the sheet: ByteRead[7:0] = ByteReadOut; clk = ClkIn;
  //   CpuWriteValue[7:0] = CpuWriteValueIn; enableValue = enableValueIn; fsmRead = fsmReadIn; isDirty = DirtyIn;
  //   Line2Mem[31:0] = Line2MemOut; Value0[7:0] = Line2MemOut[7:0]; Value1[7:0] = Line2MemOut[15:8];
  //   Value2[7:0] = Line2MemOut[23:16]; Value3[7:0] = Line2MemOut[31:24]; Byte0[7:0] = LineFromMemIn[7:0];
  //   LineFromMem[31:0] = LineFromMemIn; Byte1[7:0] = LineFromMemIn[15:8]; Byte2[7:0] = LineFromMemIn[23:16];
  //   Byte3[7:0] = LineFromMemIn[31:24]; Offset[1:0] = OffsetIn

  // Notes on the sheet:
  //   I think fsmWrite and isDirty are interchangeable here
  //   check MemWrite, contain (when ready), byte Read after read 
endmodule

module UpdateAges (
  input  [1:0] AgeOfThisWayIn,
  input  [1:0] AgeOfWayAccessedIn,
  output [1:0] NewAgeOut
);

  wire [1:0] adder_1_out, AssignIndex;
  wire [2:0] comparator_1_eq;

  Comparator #(.mode("unsigned"), .width(2)) comparator_1 (
    .a(AgeOfThisWayIn), .b(AgeOfWayAccessedIn), .eq(comparator_1_eq[0]));  // open: gt, lt
  Comparator #(.mode("unsigned"), .width(2)) comparator_2 (
    .a(AgeOfThisWayIn), .b(AgeOfWayAccessedIn), .lt(comparator_1_eq[1]));  // open: gt, eq
  Comparator #(.mode("unsigned"), .width(2)) comparator_3 (
    .a(AgeOfThisWayIn), .b(AgeOfWayAccessedIn), .gt(comparator_1_eq[2]));  // open: eq, lt
  BitFinder #(.width(3)) bitfinder_1 (.in(comparator_1_eq), .index(AssignIndex));  // open: found
  Adder #(.width(2)) adder_1 (.a(2'b01), .b(AgeOfThisWayIn), .out(adder_1_out));  // open: cin, cout
  Multiplexer #(.enable("false"), .select(2), .width(2)) multiplexer_1 (
    .in0(2'b00), .in1(adder_1_out), .in2(AgeOfThisWayIn), .out(NewAgeOut), .sel(AssignIndex));  // open: in3

  // Other names for the same wires on the sheet: AgeOfThisWay[1:0] = AgeOfThisWayIn;
  //   AgeOfWayAccessed[1:0] = AgeOfWayAccessedIn; NewAge[1:0] = NewAgeOut

  // Notes on the sheet:
  //   Update tags and ages
endmodule

module nextState (
  input  [3:0] State,
  input  Dirty,
  input  Contain,
  input  CpuRead,
  input  CpuWrite,
  output S3Next,
  output S2Next,
  output S1Next,
  output S0Next
);

  wire and_1_out, and_2_out, and_3_out, and_4_out, and_5_out, and_6_out, and_7_out, and_8_out, and_9_out,
       and_10_out, and_11_out, and_12_out, and_13_out, not_1_out, not_2_out, not_3_out, not_4_out, not_5_out,
       not_6_out;

  not not_1 (not_1_out, State[3]);
  not not_2 (not_2_out, State[2]);
  not not_3 (not_3_out, State[1]);
  not not_4 (not_4_out, State[0]);
  not not_5 (not_5_out, Dirty);
  not not_6 (not_6_out, Contain);
  and and_1 (and_1_out, not_1_out, State[1]);
  and and_2 (and_2_out, State[2], not_4_out);
  and and_3 (and_3_out, State[3], not_4_out);
  and and_4 (and_4_out, State[3], State[2], not_3_out);
  and and_5 (and_5_out, not_1_out, State[0]);
  and and_6 (and_6_out, not_1_out, State[2], not_5_out);
  and and_7 (and_7_out, State[2], State[0]);
  and and_8 (and_8_out, not_1_out, State[1], not_5_out);
  and and_9 (and_9_out, State[2], not_3_out, State[0], not_6_out);
  and and_10 (and_10_out, State[3], State[2], not_3_out, State[0]);
  and and_11 (and_11_out, not_1_out, State[0], not_6_out);
  and and_12 (and_12_out, not_1_out, State[1]);
  and and_13 (and_13_out, State[3], not_3_out);
  or or_1 (S3Next, and_1_out, and_2_out, and_3_out, and_4_out);
  or or_2 (S2Next, and_5_out, and_6_out, and_7_out);
  or or_3 (S1Next, and_8_out, and_9_out, and_10_out);
  or or_4 (S0Next, not_2_out, and_11_out, and_12_out, and_13_out);
endmodule

module OutputEquation (
  input  [3:0] NextState,
  output Ready,
  output MemRead,
  output MemWrite,
  output UpdateAge,
  output IsInit,
  output EnableValue
);

  wire and_4_out, and_5_out, and_7_out, and_8_out, not_1_out, not_2_out, not_3_out, not_4_out;

  not not_1 (not_1_out, NextState[3]);
  not not_2 (not_2_out, NextState[2]);
  not not_3 (not_3_out, NextState[1]);
  not not_4 (not_4_out, NextState[0]);
  and and_1 (Ready, not_1_out, not_2_out, NextState[0]);
  and and_2 (MemRead, NextState[3], NextState[1]);
  and and_3 (MemWrite, NextState[3], NextState[2], not_3_out, NextState[0]);
  and and_4 (and_4_out, not_1_out, not_2_out, not_3_out, not_4_out);
  or or_1 (UpdateAge, and_4_out, and_5_out);
  and and_5 (and_5_out, NextState[3], not_2_out, NextState[0]);
  and and_6 (IsInit, not_1_out, not_2_out, not_4_out);
  and and_7 (and_7_out, NextState[3], not_2_out, not_4_out);
  or or_2 (EnableValue, and_7_out, and_8_out);
  and and_8 (and_8_out, NextState[3], NextState[1]);
endmodule

module fsm (
  input  DirtyIn,
  input  ContainIn,
  input  CpuReadIn,
  input  CpuWriteIn,
  input  ClkIn,
  output ReadyOut,
  output MemReadOut,
  output MemWriteOut,
  output UpdateAgeOut,
  output IsInitOut,
  output EnableValueOut
);

  wire [3:0] nextstate_1_s0next, register_1_q;

  // Probe on register_1_q
  nextState nextstate_1 (
    .State(register_1_q), .Dirty(DirtyIn), .Contain(ContainIn), .CpuRead(CpuReadIn), .CpuWrite(CpuWriteIn),
    .S3Next(nextstate_1_s0next[3]), .S2Next(nextstate_1_s0next[2]), .S1Next(nextstate_1_s0next[1]),
    .S0Next(nextstate_1_s0next[0]));
  Register #(.width(4)) register_1 (.D(nextstate_1_s0next), .clk(ClkIn), .Q(register_1_q));  // open: en, clr
  OutputEquation outputequation_1 (
    .NextState(register_1_q), .Ready(ReadyOut), .MemRead(MemReadOut), .MemWrite(MemWriteOut),
    .UpdateAge(UpdateAgeOut), .IsInit(IsInitOut), .EnableValue(EnableValueOut));

  // Other names for the same wires on the sheet: Clk = ClkIn; Contain = ContainIn; CpuRead = CpuReadIn;
  //   CpuWrite = CpuWriteIn; Dirty = DirtyIn
endmodule
